# Fritzing sketch board (saved by Fritzing 0.9.0b)
perfboards: 1

parts:
  U1 = atmega328 [package=dip]
  D1 = Zener Diode [part_number=1N4732A breakdown_voltage=3.6V package="Melf DO-213 AB [SMD]"]
  D2 = Zener Diode [part_number=1N4732A breakdown_voltage=3.6V package="Melf DO-213 AB [SMD]"]
  12Mhz_Crystal = Crystal [frequency="16 Mhz" package=THT]
  C1 = Capacitor [package=cap-pth-small2]
  C2 = Capacitor [package=cap-pth-small2]
  R1 = Resistor [tolerance=±5% resistance=68 package=THT]
  C4 = Electrolytic Capacitor [capacitance=4.7µF voltage=20V package="200 mil [THT, electrolytic]"]
  C5_100nF = Capacitor [package=cap-pth-small-kit]
  R2 = Resistor [tolerance=±5% resistance=68 package=THT]
  S1 = Pushbutton [package="[THT]"]
  S2 = SWITCH_SPDT [package=kps-1290]
  R3 = Resistor [tolerance=±5% resistance=1.5k package=THT]
  R4 = Resistor [tolerance=±5% resistance=10k package=THT]
  J1 = single row smd female pin header, 15 pins [form="♀ (female)"]  # not connected
  USB_connector = USB connector [package=THT]

nets:
  N1: U1.RESET, S1.Pin_1, S1.Pin_2, R4.Pin_0
  N2: U1.D2, R1.Pin_0
  VCC: U1.VCC, U1.AVCC, U1.AREF, C4.+, C5_100nF.1, R3.Pin_0, R4.Pin_1, USB_connector.5V
  GND: U1.GND, D1.anode, D2.anode, C1.2, C2.1, C4.-, C5_100nF.2, S1.Pin_3, S1.Pin_4, S2.S, USB_connector.GND, USB_connector.chassis5, USB_connector.chassis6
  N3: U1.XLAT1, 12Mhz_Crystal.pin_0, C2.2
  N4: U1.XLAT2, 12Mhz_Crystal.pin_1, C1.1
  N5: U1.D7, R2.Pin_0
  N6: D1.cathode, R2.Pin_1, S2.O, S2.P, R3.Pin_1, USB_connector.d-
  N7: D2.cathode, R1.Pin_1, USB_connector.d+

notes:
  Bootloader
  switch
  D+
  D-
  D- pull-up
  Reset
  switch
  5V stabilization
  Reset
  pull-up
  5V / VCC
